# Fritzing sketch motors (saved by Fritzing 0.9.3b)
circuit board: 8.46667cm x 5.64444cm
breadboards: 1

parts:
  IC1 = L293D [package=THT]
  Power_plug1 = Power plug
  Componente1 = Arduino Uno (Rev3)

nets:
  N1: IC1.Enable_1, IC1.Enable_2, IC1.+V, Componente1.5V
  N2: IC1.0V, Componente1.GND
  N3: IC1.+Vmotor, Power_plug1.VCC
